// Logisim project 53_Németh.circ as structural Verilog: 1 circuit, main circuit main
module main (
  input  A,
  input  B,
  input  C,
  input  D,
  output A_D,
  output B_D,
  output C_D,
  output D_D,
  output A_K,
  output B_K,
  output C_K,
  output D_K
);

  wire n_a_b_out, n_b_c_d_out, n_b_c_nd_out, n_b_d_out, n_b_nc_nd_out, n_c_d_nb_out, n_c_d_out, n_c_nd_out,
       n_nb_c_nd_out, n_nb_d_out, n_nb_nc_out, n_nb_nd_out, n_nc_d_out, n_nc_nd_out, na_out, nb_2_out,
       nb_out, nc_2_out, nc_out, nd_2_out, nd_out;

  nand na (na_out, A, A);
  nand nd (nd_out, D, D);
  nand nb (nb_out, B, B);
  nor nb_2 (nb_2_out, B, B);
  nand nc (nc_out, C, C);
  nor nc_2 (nc_2_out, C, C);
  nor nd_2 (nd_2_out, D, D);
  nand n_b_d (n_b_d_out, B, D);
  nand n_b_c_nd (n_b_c_nd_out, B, C, nd_out);
  nand n_b_nc_nd (n_b_nc_nd_out, B, nc_out, nd_out);
  nand n_nb_c_nd (n_nb_c_nd_out, nb_out, C, nd_out);
  nand n_nb_d (n_nb_d_out, nb_out, D);
  nand n_nc_nd (n_nc_nd_out, nc_out, nd_out);
  nand n_c_d (n_c_d_out, C, D);
  nor n_a_b (n_a_b_out, A, B);
  nor n_c_d_nb (n_c_d_nb_out, nb_2_out, C, D);
  nor n_nb_nd (n_nb_nd_out, nb_2_out, nd_2_out);
  nor n_nb_nc (n_nb_nc_out, nb_2_out, nc_2_out);
  nor n_b_c_d (n_b_c_d_out, B, C, D);
  nor n_c_nd (n_c_nd_out, nd_2_out, C);
  nor n_nc_d (n_nc_d_out, nc_2_out, D);
  nand n_na_n_b_d__n_b_c_nd (A_D, n_b_d_out, na_out, n_b_c_nd_out);
  nand n_n_b_nc_nd__n_nb_c_nd__n_nb_c (B_D, n_b_nc_nd_out, n_nb_c_nd_out, n_nb_d_out);
  nand n_n_c_d__n_nc_nd (C_D, n_nc_nd_out, n_c_d_out);
  nand n_n_nb_c_nd__n_b_c_nd__n_nc_nd (D_D, n_b_c_nd_out, n_nc_nd_out, n_nb_c_nd_out);
  nor n_n_a_b__n_c_d_nb (A_K, n_a_b_out, n_c_d_nb_out);
  nor n_n_nb_nd__n_nb_nc__n_b_c_d (B_K, n_nb_nd_out, n_nb_nc_out, n_b_c_d_out);
  nor n_n_c_nd__n_nc_d (C_K, n_c_nd_out, n_nc_d_out);
  not nd_3 (D_K, D);  // NOR_Gate
endmodule
